# Fritzing sketch circuit_diagram (saved by Fritzing 1.0.4)
breadboards: 1

parts:
  S1 = Pushbutton [package="[THT]"]
  S2 = Pushbutton [package="[THT]"]
  LED1 = RGB LED (com. cathode, rgb) [color="Red (633nm)" current=0.030A package="5 mm [THT]"]
  R1 = Resistor [tolerance=±5% power=0.25W resistance=220 package=THT]
  R2 = Resistor [tolerance=±5% power=0.25W resistance=220 package=THT]
  R3 = Resistor [tolerance=±5% power=0.25W resistance=220 package=THT]
  M1 = MakerFocus MAX30102
  A1 = MYOWARE Muscle sensor
  A2 = AVR-IOT-WX
  U1 = Vibration Motor- ROB-08449 [package=vibe-motor-10mm]

nets:
  N1: S1.Pin_1, S1.Pin_2, S2.Pin_1, S2.Pin_2, LED1.green_anode, M1.VIN, A1.Pin_5, A2.Pin_1, A2.Pin_10, U1.+
  N2: S1.Pin_3, S1.Pin_4, A2.Pin_8
  N3: S2.Pin_3, S2.Pin_4, A2.Pin_6
  N4: LED1.red_anode, R3.Pin_1
  N5: LED1.common_cathode, R2.Pin_1
  N6: LED1.blue_anode, R1.Pin_1
  N7: R1.Pin_0, A2.Pin_5
  N8: R2.Pin_0, A2.Pin_4
  N9: R3.Pin_0, A2.Pin_3
  N10: M1.GND, A1.Pin_4, A2.Pin_9
  N11: M1.SCL, A2.Pin_14
  N12: M1.SDA, A2.Pin_13
  N13: A1.Pin_6, A2.Pin_18
  N14: A2.Pin_7, U1.-

custom parts:
  MakerFocus MAX30102: Oximeter module using the MAX30102 chip. As usual, if you want the mounting holes in pcb, you need to drag a hole over the pad in silkscreen to actually drill the hole (by default they are not drilled)
  MYOWARE Muscle sensor: The MyoWare® 2.0 Muscle Sensor is an Arduino-compatible, all-in-one electromyography (EMG) sensor from Advancer Technologies.
  AVR-IOT-WX: The AVR-IoT WG development board combines a powerful ATmega4808 AVR® MCU, an ATECC608A CryptoAuthentication™ secure element IC and the fully certified ATWINC1510 Wi-Fi® network controller.
